// Digital circuit control-unit.dig as structural Verilog
module control_unit (
  input  [6:0] opcode,
  input  [2:0] funct3,
  input  [6:0] funct7,
  output RegWrite,
  output ALUSrc,
  output [1:0] ImmSrc,
  output [3:0] ALUOperation
);

  wire add, addi, \and , andi, comparator_2_eq, comparator_3_eq, comparator_4_eq, comparator_5_eq,
       comparator_6_eq, comparator_7_eq, comparator_8_eq, comparator_9_eq, comparator_10_eq,
       comparator_11_eq, comparator_13_eq, comparator_14_eq, comparator_15_eq, itype, \or , rtype, slt, slti,
       sub;
  wire [2:0] priorityencoder_1_num;

  ROM #(.AddrBits(3), .Bits(8)) rom_1 (
    .A(priorityencoder_1_num), .sel(1'b1), .D({ALUOperation, ImmSrc, ALUSrc, RegWrite}));
  Comparator #(.Bits(7)) comparator_1 (.a(opcode), .b(7'b0110011), .eq(rtype));  // open: gt, lt
  Comparator #(.Bits(3)) comparator_2 (.a(funct3), .b(3'b000), .eq(comparator_2_eq));  // open: gt, lt
  Comparator #(.Bits(7)) comparator_3 (.a(funct7), .b({7{1'b0}}), .eq(comparator_3_eq));  // open: gt, lt
  Comparator #(.Bits(3)) comparator_4 (.a(funct3), .b(3'b000), .eq(comparator_4_eq));  // open: gt, lt
  Comparator #(.Bits(7)) comparator_5 (.a(funct7), .b(7'b0100000), .eq(comparator_5_eq));  // open: gt, lt
  Comparator #(.Bits(3)) comparator_6 (.a(funct3), .b(3'b111), .eq(comparator_6_eq));  // open: gt, lt
  Comparator #(.Bits(7)) comparator_7 (.a(funct7), .b({7{1'b0}}), .eq(comparator_7_eq));  // open: gt, lt
  Comparator #(.Bits(3)) comparator_8 (.a(funct3), .b(3'b110), .eq(comparator_8_eq));  // open: gt, lt
  Comparator #(.Bits(7)) comparator_9 (.a(funct7), .b({7{1'b0}}), .eq(comparator_9_eq));  // open: gt, lt
  Comparator #(.Bits(3)) comparator_10 (.a(funct3), .b(3'b010), .eq(comparator_10_eq));  // open: gt, lt
  Comparator #(.Bits(7)) comparator_11 (.a(funct7), .b({7{1'b0}}), .eq(comparator_11_eq));  // open: gt, lt
  Comparator #(.Bits(7)) comparator_12 (.a(opcode), .b(7'b0010011), .eq(itype));  // open: gt, lt
  Comparator #(.Bits(3)) comparator_13 (.a(funct3), .b(3'b000), .eq(comparator_13_eq));  // open: gt, lt
  Comparator #(.Bits(3)) comparator_14 (.a(funct3), .b(3'b010), .eq(comparator_14_eq));  // open: gt, lt
  Comparator #(.Bits(3)) comparator_15 (.a(funct3), .b(3'b111), .eq(comparator_15_eq));  // open: gt, lt
  and and_1 (add, comparator_2_eq, rtype, comparator_3_eq);
  and and_2 (sub, comparator_4_eq, rtype, comparator_5_eq);
  and and_3 (\and , comparator_6_eq, rtype, comparator_7_eq);
  and and_4 (\or , comparator_8_eq, rtype, comparator_9_eq);
  and and_5 (slt, comparator_10_eq, rtype, comparator_11_eq);
  and and_6 (addi, itype, comparator_13_eq);
  and and_7 (slti, itype, comparator_14_eq);
  and and_8 (andi, itype, comparator_15_eq);
  PriorityEncoder #(.Selector_Bits(3)) priorityencoder_1 (
    .in0(add), .in1(sub), .in2(\and ), .in3(\or ), .in4(slt), .in5(addi), .in6(slti), .in7(andi),
    .num(priorityencoder_1_num));  // open: any

  // Other names for the same wires on the sheet: f3[2:0] = funct3; f7[6:0] = funct7; oc[6:0] = opcode

  // Notes on the sheet:
  //   contents of rom_1 (hex, n*v repeats v):
  //   82,86,80,81,87,c2,c7
endmodule
