// Digital circuit cpu.dig as structural Verilog
module cpu (
  input  clk,
  output [31:0] ReadData1,
  output [31:0] ReadData2
);

  wire alu_1_p3, aluA, control_unit_1_p4, control_unit_1_p5;
  wire [2:0] f3;
  wire [4:0] rd;
  wire [6:0] f7, oc;
  wire [31:0] add_1_s, bitextender_1_out, control_unit_1_p8, multiplexer_1_out, PC_q, wd;

  BitExtender #(.inputBits(12), .outputBits(32)) bitextender_1 (.in({f7, ReadData2[4:0]}), .out(bitextender_1_out));
  Multiplexer #(.Bits(32)) multiplexer_1 (
    .sel(control_unit_1_p5), .in_0(control_unit_1_p8), .in_1(bitextender_1_out), .out(multiplexer_1_out));
  Register #(.Bits(32), .isProgramCounter("true")) PC (.D(add_1_s), .C(clk), .en(1'b1), .Q(PC_q));
  Add #(.Bits(32)) add_1 (.a(32'h4), .b(PC_q), .c_i(1'b0), .s(add_1_s));  // open: c_o
  // alu alu_1: pin names not known; wires that end beside it: aluA, multiplexer_1_out, alu_1_p3, wd
  ROM #(.AddrBits(10), .isProgramMemory("true"), .Bits(32)) Instruction_Memory (
    .A(PC_q[11:2]), .sel(1'b1), .D({f7, ReadData2[4:0], ReadData1[4:0], f3, rd, oc}));
  // control_unit control_unit_1: pin names not known; wires that end beside it: oc, f3, f7, control_unit_1_p4, control_unit_1_p5, alu_1_p3, aluA, control_unit_1_p8
  register_file register_file_1 (
    .ReadReg1(ReadData1[4:0]), .ReadReg2(ReadData2[4:0]), .WriteReg(rd), .WriteData(wd),
    .RegWrite(control_unit_1_p4), .Clock(clk));  // open: ReadData1, ReadData2
  // Pins of 5 and 32 bits meet at ReadData1
  // Pins of 5 and 32 bits meet at ReadData2

  // Other names for the same wires on the sheet: rs1[31:0] = ReadData1; imm[11:0] = {f7, ReadData2[4:0]};
  //   rs2[31:0] = ReadData2; clock = clk

  // Notes on the sheet:
  //   contents of Instruction_Memory (hex, n*v repeats v):
  //   20040005,2008000f,882020,843820,884825,e95025
endmodule

/* Test case cpu:
clk ReadData1 ReadData2
0 0 0		# addi $4 $0 -20
C (-20) 0 	# addi $5 $4 0x7FFF
C 32747 0 	# addi $6 $5 0x7018
C 61443 0 	# addi $7 $6 0x5311
C 0 0 		# ori $10 $0 10
C 10 0 		# ori $11 $10 0xFF55
C 65375 0 	# ori $12 $11 39
C 61443 0 	# andi $14 $6 0xE123
C 57347 0 	# andi $15 $14 0xFF1C
C 57344 0 	# andi $17 $15 0x541
C (-20) 0 	# slti $18 $4 311
C 1 0 		# slti $19 $18 2
C 1 0 		# slti $20 $19 0
C 0 0 		# slti $21 $20 -3	
C 0 0 		# slti $22 $21 5 
C 1 0 		# addi $0 $22 0 
C (-20) 0 	# slti $23 $4 -20	
C 0 0 		# addi $0 $23 0
C 65375 0 	# slti $24 $11 -90 
C 0 0 		# addi $0 $24 0
C (-20) 0 	# slti $25 $4 0 
C 1 0 		# addi $0 $25 0 
C 65375 0 	# slti $26 $11 6000
C 0 0 		# addi $0 $26 0 
C (-20) 0 	# slti $27 $4 -1 
C 1 0 		# addi $0 $27 0	
*/
